// Digital circuit Branch Unit.dig as structural Verilog
module Branch_Unit (
  input  [31:0] A,
  input  [31:0] B,
  input  [4:0] BrOp,
  output NxtPCSrc
);

  wire comparator_1_eq, comparator_1_lt, comparator_2_lt, multiplexer_1_out, not_1_out, not_2_out, not_3_out;

  Comparator #(.Signed("true"), .Bits(32)) comparator_1 (
    .a(A), .b(B), .eq(comparator_1_eq), .lt(comparator_1_lt));  // open: gt
  Comparator #(.Bits(32)) comparator_2 (.a(A), .b(B), .lt(comparator_2_lt));  // open: gt, eq
  not not_1 (not_1_out, comparator_2_lt);
  not not_2 (not_2_out, comparator_1_lt);
  not not_3 (not_3_out, comparator_1_eq);
  Multiplexer #(.Selector_Bits(3)) multiplexer_1 (
    .sel(BrOp[2:0]), .in_0(comparator_1_eq), .in_1(not_3_out), .in_2(not_3_out), .in_3(comparator_1_lt),
    .in_4(comparator_1_lt), .in_5(not_2_out), .in_6(comparator_2_lt), .in_7(not_1_out),
    .out(multiplexer_1_out));
  Multiplexer #(.Selector_Bits(2)) multiplexer_2 (
    .sel(BrOp[4:3]), .in_0(1'b0), .in_1(multiplexer_1_out), .in_2(1'b1), .in_3(1'b1), .out(NxtPCSrc));
endmodule
