// Digital circuit CU.dig as structural Verilog
module CU (
  input  [6:0] OpCode,
  input  [2:0] func3,
  input  [6:0] func7,
  output RUWE,
  output [2:0] immSrc,
  output ALUASrc,
  output ALUBSrc,
  output DMWr,
  output [2:0] DMCtrl,
  output [1:0] RUWrSrc,
  output [3:0] ALUOp,
  output [4:0] BrOp
);

  wire and_1_out, and_2_out, and_3_out, and_4_out, and_5_out, and_7_out, and_8_out, not_1_out, not_3_out,
       not_4_out, not_5_out;
  wire [1:0] not_2_out;

  not not_1 (not_1_out, OpCode[6]);
  not not_2 (not_2_out[0], OpCode[5]);
  not not_3 (not_3_out, OpCode[4]);
  not not_4 (not_4_out, OpCode[3]);
  not not_5 (not_5_out, OpCode[2]);
  and and_1 (and_1_out, not_2_out[0], not_5_out);
  and and_2 (and_2_out, not_3_out, not_4_out, OpCode[2]);
  and and_3 (and_3_out, OpCode[4], not_5_out);
  and and_4 (and_4_out, OpCode[6], not_5_out);
  and and_5 (and_5_out, OpCode[4], OpCode[2]);
  and and_6 (immSrc[0], OpCode[5], not_5_out);
  and and_7 (and_7_out, not_1_out, OpCode[2]);
  and and_8 (and_8_out, OpCode[6], not_5_out);
  and and_9 (RUWrSrc[1], not_3_out, OpCode[2]);
  and and_10 (RUWrSrc[0], not_3_out, not_5_out);
  or or_1 (not_2_out[1], not_3_out, OpCode[2]);
  and and_11 (BrOp[4], not_3_out, OpCode[2]);
  or or_2 (RUWE, and_1_out, and_2_out, and_3_out);
  or or_3 (immSrc[2], and_4_out, OpCode[3]);
  or or_4 (immSrc[1], and_5_out, OpCode[3]);
  or or_5 (ALUASrc, and_7_out, and_8_out, OpCode[3]);
  or or_6 (ALUBSrc, not_2_out[0], not_3_out, OpCode[2]);
  and and_12 (DMWr, not_1_out, OpCode[5], not_3_out);
  Multiplexer #(.Selector_Bits(2), .Bits(4)) multiplexer_1 (
    .sel(not_2_out), .in_0({func7[5], func3}), .in_1({1'b0, func3}), .in_2(4'b0000), .in_3(4'b0000),
    .out(ALUOp));

  assign BrOp[3:0] = {OpCode[6], func3};
  assign DMCtrl = func3;

  // Other names for the same wires on the sheet: UpBrOp[1:0] = {BrOp[4], OpCode[6]}; ALUOp1[3:0] = {func7[5], func3};
  //   ALUOp2[2:0] = func3
endmodule
