// Digital circuit Inst-Decoder.dig as structural Verilog
module Inst_Decoder (
  input  [31:0] Ins,
  output [6:0] OC,
  output [2:0] Func3,
  output [6:0] Func7,
  output [4:0] rs1,
  output [4:0] rs2,
  output [4:0] rd,
  output [24:0] imm
);


  assign Func3 = Ins[14:12];
  assign Func7 = Ins[31:25];
  assign imm = Ins[31:7];
  assign OC = Ins[6:0];
  assign rd = Ins[11:7];
  assign rs1 = Ins[19:15];
  assign rs2 = Ins[24:20];
endmodule
