// Digital circuit Memoria.dig as structural Verilog
module Memoria (
  input  [31:0] addr,
  input  [31:0] DataW,
  input  WE,
  input  [2:0] DMCtrl,
  output [31:0] DataR
);

  wire [31:0] bitextender_1_out, bitextender_2_out, multiplexer_1_out, ramasync_1_q;

  Multiplexer #(.Selector_Bits(2), .Bits(32)) multiplexer_1 (
    .sel(DMCtrl[1:0]), .in_0({{24{1'b0}}, DataW[7:0]}), .in_1({{16{1'b0}}, DataW[15:0]}), .in_2(DataW),
    .in_3(DataW), .out(multiplexer_1_out));
  RAMAsync #(.AddrBits(24), .Bits(32)) ramasync_1 (.A(addr[23:0]), .D(multiplexer_1_out), .we(WE), .Q(ramasync_1_q));
  BitExtender #(.outputBits(32)) bitextender_1 (.in(ramasync_1_q[7:0]), .out(bitextender_1_out));
  BitExtender #(.inputBits(16), .outputBits(32)) bitextender_2 (.in(ramasync_1_q[15:0]), .out(bitextender_2_out));
  Multiplexer #(.Selector_Bits(3), .Bits(32)) multiplexer_2 (
    .sel(DMCtrl), .in_0(bitextender_1_out), .in_1(bitextender_2_out), .in_2(ramasync_1_q),
    .in_3(ramasync_1_q), .in_4({{24{1'b0}}, ramasync_1_q[7:0]}), .in_5({{16{1'b0}}, ramasync_1_q[15:0]}),
    .in_6({{16{1'b0}}, ramasync_1_q[15:0]}), .in_7({{16{1'b0}}, ramasync_1_q[15:0]}), .out(DataR));
endmodule
