// Digital circuit RISC-V.dig as structural Verilog
module RISC_V (
  input  clk
);

  wire ALUASrc, ALUBSrc, branch_unit_1_nxtpcsrc, DMWr, RUWE;
  wire [1:0] RUWrSrc;
  wire [2:0] DMCtrl, immSrc, inst_decoder_1_func3;
  wire [3:0] ALUOp;
  wire [4:0] cu_1_brop, inst_decoder_1_rd, inst_decoder_1_rs1, inst_decoder_1_rs2;
  wire [6:0] inst_decoder_1_func7, inst_decoder_1_oc;
  wire [23:0] add_1_s, calu_1_alures, multiplexer_3_out, PC_q;
  wire [24:0] inst_decoder_1_imm;
  wire [31:0] bitextender_1_out, immgen_1_imm_ext, Inst_RAM_d, memoria_1_datar, multiplexer_1_out,
       multiplexer_2_out, multiplexer_4_out, RU_da, RU_db;
  wire [31:24] calu_1_alures_2;

  Register #(.Bits(24), .isProgramCounter("true")) PC (.D(multiplexer_3_out), .C(clk), .en(1'b1), .Q(PC_q));
  Add #(.Bits(24)) add_1 (.a(24'h1), .b(PC_q), .c_i(1'b0), .s(add_1_s));  // open: c_o
  ROM #(.AddrBits(24), .Bits(32)) Inst_RAM (.A(PC_q), .sel(1'b1), .D(Inst_RAM_d));
  Inst_Decoder inst_decoder_1 (
    .Ins(Inst_RAM_d), .OC(inst_decoder_1_oc), .Func3(inst_decoder_1_func3), .Func7(inst_decoder_1_func7),
    .rd(inst_decoder_1_rd), .rs1(inst_decoder_1_rs1), .rs2(inst_decoder_1_rs2), .imm(inst_decoder_1_imm));
  CU cu_1 (
    .OpCode(inst_decoder_1_oc), .func3(inst_decoder_1_func3), .func7(inst_decoder_1_func7), .RUWE(RUWE),
    .immSrc(immSrc), .ALUASrc(ALUASrc), .ALUBSrc(ALUBSrc), .DMWr(DMWr), .DMCtrl(DMCtrl), .RUWrSrc(RUWrSrc),
    .ALUOp(ALUOp), .BrOp(cu_1_brop));
  BitExtender #(.inputBits(24), .outputBits(32)) bitextender_1 (.in(PC_q), .out(bitextender_1_out));
  immGen immgen_1 (.imm(inst_decoder_1_imm), .immSrc(immSrc), .imm_Ext(immgen_1_imm_ext));
  RegisterFile #(.AddrBits(5), .Bits(32)) RU (
    .Din(multiplexer_4_out), .we(RUWE), .Rw(inst_decoder_1_rd), .C(clk), .Ra(inst_decoder_1_rs1),
    .Rb(inst_decoder_1_rs2), .Da(RU_da), .Db(RU_db));
  Multiplexer #(.Bits(32)) multiplexer_1 (
    .sel(ALUASrc), .in_0(RU_da), .in_1(bitextender_1_out), .out(multiplexer_1_out));
  Multiplexer #(.Bits(32)) multiplexer_2 (
    .sel(ALUBSrc), .in_0(RU_db), .in_1(immgen_1_imm_ext), .out(multiplexer_2_out));
  Branch_Unit branch_unit_1 (
    .A(multiplexer_1_out), .B(multiplexer_2_out), .BrOp(cu_1_brop), .NxtPCSrc(branch_unit_1_nxtpcsrc));
  cALU calu_1 (.ALUOp(ALUOp), .A(multiplexer_1_out), .B(multiplexer_2_out), .ALURes({calu_1_alures_2, calu_1_alures}));
  Multiplexer #(.Bits(24)) multiplexer_3 (
    .sel(branch_unit_1_nxtpcsrc), .in_0(add_1_s), .in_1(calu_1_alures), .out(multiplexer_3_out));
  Memoria memoria_1 (
    .addr({calu_1_alures_2, calu_1_alures}), .DataW(RU_db), .WE(DMWr), .DMCtrl(DMCtrl),
    .DataR(memoria_1_datar));
  Multiplexer #(.Selector_Bits(2), .Bits(32)) multiplexer_4 (
    .sel(RUWrSrc), .in_0({calu_1_alures_2, calu_1_alures}), .in_1(memoria_1_datar),
    .in_2({{8{1'b0}}, add_1_s}), .in_3({{8{1'b0}}, add_1_s}), .out(multiplexer_4_out));

  // Notes on the sheet:
  //   contents of Inst_RAM (hex, n*v repeats v):
  //   1930293,6283b3,728333
endmodule
