// Digital circuit cALU.dig as structural Verilog
module cALU (
  input  [3:0] ALUOp,
  input  [31:0] A,
  input  [31:0] B,
  output [31:0] ALURes
);

  wire [0:0] comparator_1_eq, comparator_2_eq;
  wire [31:0] add_1_s, and_1_out, barrelshifter_1_out, barrelshifter_2_out, barrelshifter_3_out,
       multiplexer_1_out, multiplexer_2_out, or_1_out, sub_1_s, xor_1_out;

  Add #(.Bits(32)) add_1 (.a(A), .b(B), .c_i(1'b0), .s(add_1_s));  // open: c_o
  Sub #(.Bits(32)) sub_1 (.a(A), .b(B), .c_i(1'b0), .s(sub_1_s));  // open: c_o
  BarrelShifter #(.Bits(32)) barrelshifter_1 (.in(A), .shift(B[5:0]), .out(barrelshifter_1_out));
  Comparator #(.Signed("true"), .Bits(32)) comparator_1 (.a(A), .b(B), .eq(comparator_1_eq[0]));  // open: gt, lt
  Comparator #(.Bits(32)) comparator_2 (.a(A), .b(B), .eq(comparator_2_eq[0]));  // open: gt, lt
  assign xor_1_out = A ^ B;  // XOr xor_1, 32 bits wide
  BarrelShifter #(.Bits(32), .direction("right")) barrelshifter_2 (.in(A), .shift(B[5:0]), .out(barrelshifter_2_out));
  BarrelShifter #(.barrelShifterMode("arithmetic"), .Bits(32), .direction("right")) barrelshifter_3 (
    .in(A), .shift(B[5:0]), .out(barrelshifter_3_out));
  assign or_1_out = A | B;  // Or or_1, 32 bits wide
  assign and_1_out = A & B;  // And and_1, 32 bits wide
  Multiplexer #(.Bits(32)) multiplexer_1 (.sel(ALUOp[3]), .in_0(add_1_s), .in_1(sub_1_s), .out(multiplexer_1_out));
  Multiplexer #(.Bits(32)) multiplexer_2 (
    .sel(ALUOp[3]), .in_0(barrelshifter_2_out), .in_1(barrelshifter_3_out), .out(multiplexer_2_out));
  Multiplexer #(.Selector_Bits(3), .Bits(32)) multiplexer_3 (
    .sel(ALUOp[2:0]), .in_0(multiplexer_1_out), .in_1(barrelshifter_1_out),
    .in_2({{31{1'b0}}, comparator_1_eq[0]}), .in_3({{31{1'b0}}, comparator_2_eq[0]}), .in_4(xor_1_out),
    .in_5(multiplexer_2_out), .in_6(or_1_out), .in_7(and_1_out), .out(ALURes));
endmodule
