// Digital circuit immGen.dig as structural Verilog
module immGen (
  input  [24:0] imm,
  input  [2:0] immSrc,
  output [31:0] imm_Ext
);

  wire [11:0] bitextender_4_out, bitextender_5_out;
  wire [19:0] bitextender_3_out;
  wire [20:0] bitextender_1_out, bitextender_2_out;

  BitExtender #(.inputBits(1), .outputBits(21)) bitextender_1 (.in(imm[24]), .out(bitextender_1_out));
  BitExtender #(.inputBits(1), .outputBits(21)) bitextender_2 (.in(imm[24]), .out(bitextender_2_out));
  BitExtender #(.inputBits(1), .outputBits(20)) bitextender_3 (.in(imm[24]), .out(bitextender_3_out));
  BitExtender #(.inputBits(1), .outputBits(12)) bitextender_4 (.in(1'b0), .out(bitextender_4_out));
  BitExtender #(.inputBits(1), .outputBits(12)) bitextender_5 (.in(imm[24]), .out(bitextender_5_out));
  Multiplexer #(.Bits(32), .Selector_Bits(3)) multiplexer_1 (
    .sel(immSrc), .in_0({bitextender_1_out, imm[23:13]}), .in_1({bitextender_2_out, imm[23:18], imm[4:0]}),
    .in_2({imm[24:5], bitextender_4_out}), .in_3({imm[24:5], bitextender_4_out}),
    .in_4({bitextender_3_out, imm[0], imm[23:18], imm[4:1], 1'b0}),
    .in_5({bitextender_3_out, imm[0], imm[23:18], imm[4:1], 1'b0}),
    .in_6({bitextender_5_out, imm[12:5], imm[13], imm[23:14], 1'b0}),
    .in_7({bitextender_5_out, imm[12:5], imm[13], imm[23:14], 1'b0}), .out(imm_Ext));

  // Notes on the sheet:
  //   31
  //   30:25
  //   24:21
  //   20
  //   19:12
  //   7
  //   11:8
endmodule
